# Fritzing sketch interrupt_switch_wiring (saved by Fritzing 0.9.2b)
breadboards: 1

parts:
  Part1 = Arduino Uno (Rev3)
  S1 = Pushbutton [package="[THT]"]
  S2 = Pushbutton [package="[THT]"]
  R1 = Resistor [tolerance=±5% resistance=1k package=THT]
  R2 = Resistor [tolerance=±5% resistance=1k package=THT]

nets:
  N1: Part1.A0, S2.Pin_1, S2.Pin_2, R1.Pin_0
  N2: Part1.A1, S1.Pin_3, S1.Pin_4, R2.Pin_0
  N3: Part1.3V3, S1.Pin_1, S1.Pin_2, S2.Pin_3, S2.Pin_4
  N4: Part1.GND, R1.Pin_1, R2.Pin_1
